// Logisim project ARBITER.circ as structural Verilog: 4 circuits, main circuit main
module main (
);

  wire and_1_out, and_2_out, and_3_out, and_4_out, and_5_out, Backup_out, clock_1_out, clock_2_out,
       clock_3_out, clock_4_out, clock_5_out, clock_6_out, clock_7_out, counter_1_carry, counter_2_carry,
       Counter_Down_pin1, Counter_Down_pin3, Counter_Down_pin7, Counter_Down_pin15, Counter_UP_pin3,
       Counter_UP_pin7, Counter_UP_pin15, dipswitch_1_sw1, dipswitch_1_sw2, dipswitch_2_sw1, dipswitch_2_sw2,
       dipswitch_3_sw1, dipswitch_3_sw2, Latcher_pin2, Latcher_pin5, Master_out, N_OR_pin3, N_OR_pin4,
       N_OR_pin8, N_OR_pin9, N_OR_pin10, not_1_out, not_2_out, not_3_out, not_4_out, not_5_out, not_6_out,
       not_7_out, not_8_out, not_9_out, not_10_out, not_11_out, not_12_out, or_1_out, or_2_out, or_3_out,
       or_4_out, or_6_out, or_7_out, or_8_out, or_9_out, Restore_Trig_pin2, Restore_Trig_pin4,
       Restore_Trig_pin10, Restore_Trig_pin12, s_r_ff_1_q, s_r_ff_2_q, s_r_ff_3_q, t_ff_1_qn, t_ff_2_qn,
       t_ff_3_q, t_ff_3_qn, t_ff_4_q, t_ff_4_qn, t_ff_5_q, t_ff_6_q, t_ff_7_q, t_ff_8_q, t_ff_9_q, t_ff_10_q,
       t_ff_11_q, t_ff_12_q, t_ff_13_q, t_ff_14_q;
  wire [3:0] Counter_Down_pin14, Counter_UP_pin14;

  DipSwitch #(.number(2)) dipswitch_1 (.sw1(dipswitch_1_sw1), .sw2(dipswitch_1_sw2));
  Clock Backup (.out(Backup_out));
  Clock #(.highDuration(6), .lowDuration(6)) Master (.out(Master_out));
  and and_1 (and_1_out, Master_out, not_1_out);
  not not_1 (not_1_out, dipswitch_1_sw1);
  Clock #(.highDuration(4), .lowDuration(4)) clock_1 (.out(clock_1_out));
  Clock #(.phaseOffset(1)) clock_2 (.out(clock_2_out));
  not not_2 (not_2_out, dipswitch_2_sw1);
  DipSwitch #(.number(2)) dipswitch_2 (.sw1(dipswitch_2_sw1), .sw2(dipswitch_2_sw2));
  Clock clock_3 (.out(clock_3_out));
  Clock #(.highDuration(2), .lowDuration(2), .phaseOffset(1)) clock_4 (.out(clock_4_out));
  not not_3 (not_3_out, dipswitch_3_sw1);
  DipSwitch #(.number(2)) dipswitch_3 (.sw1(dipswitch_3_sw1), .sw2(dipswitch_3_sw2));
  LED led_1 (.in(or_1_out));
  or or_1 (or_1_out, and_1_out, dipswitch_1_sw2);
  LED led_2 (.in(Backup_out));
  LED led_3 (.in(or_2_out));
  and and_2 (and_2_out, clock_1_out, not_2_out);
  or or_2 (or_2_out, and_2_out, dipswitch_2_sw2);
  LED led_4 (.in(clock_2_out));
  and and_3 (and_3_out, clock_3_out, not_3_out);
  or or_3 (or_3_out, and_3_out, dipswitch_3_sw2);
  not not_4 (not_4_out, or_1_out);
  not not_5 (not_5_out, or_2_out);
  LED led_5 (.in(or_3_out));
  LED led_6 (.in(clock_4_out));
  Counter #(.max('h7), .width(3)) counter_1 (
    .carry(counter_1_carry), .clk(Backup_out), .clr(not_4_out));  // open: load, D, count, Q, up
  Counter #(.max('h7), .width(3)) counter_2 (
    .carry(counter_2_carry), .clk(Backup_out), .clr(or_1_out));  // open: load, D, count, Q, up
  _74161 Counter_UP (
    .pin1(or_1_out), .pin2(Backup_out), .pin3(Counter_UP_pin3), .pin4(Counter_UP_pin3),
    .pin5(Counter_UP_pin3), .pin6(Counter_UP_pin3), .pin7(Counter_UP_pin7), .pin15(Counter_UP_pin15),
    .pin14(Counter_UP_pin14[0]), .pin13(Counter_UP_pin14[1]), .pin12(Counter_UP_pin14[2]),
    .pin11(Counter_UP_pin14[3]), .pin10(Counter_UP_pin7), .pin9(Counter_UP_pin7));
  _74161 Counter_Down (
    .pin1(Counter_Down_pin1), .pin2(Backup_out), .pin3(Counter_Down_pin3), .pin4(Counter_Down_pin3),
    .pin5(Counter_Down_pin3), .pin6(Counter_Down_pin3), .pin7(Counter_Down_pin7), .pin15(Counter_Down_pin15),
    .pin14(Counter_Down_pin14[0]), .pin13(Counter_Down_pin14[1]), .pin12(Counter_Down_pin14[2]),
    .pin11(Counter_Down_pin14[3]), .pin10(Counter_Down_pin7), .pin9(Counter_Down_pin7));
  T_Flip_Flop t_ff_1 (.clk(clock_2_out), .T(1'b1), .Qn(t_ff_1_qn), .reset(not_5_out));  // open: Q, preset
  T_Flip_Flop t_ff_2 (.clk(clock_2_out), .T(1'b1), .Qn(t_ff_2_qn), .reset(or_2_out));  // open: Q, preset
  T_Flip_Flop t_ff_3 (.clk(clock_4_out), .T(1'b1), .Q(t_ff_3_q), .Qn(t_ff_3_qn), .reset(not_6_out));  // open: preset
  not not_6 (not_6_out, or_3_out);
  T_Flip_Flop t_ff_4 (.clk(clock_4_out), .T(1'b1), .Q(t_ff_4_q), .Qn(t_ff_4_qn), .reset(or_3_out));  // open: preset
  or or_4 (or_4_out, counter_1_carry, counter_2_carry);
  not not_7 (not_7_out, or_1_out);
  Hex_Digit_Display hex_digit_display_1 (.value(Counter_UP_pin14));  // open: dp
  Hex_Digit_Display hex_digit_display_2 (.value(Counter_Down_pin14));  // open: dp
  T_Flip_Flop t_ff_5 (.clk(t_ff_1_qn), .T(1'b1), .Q(t_ff_5_q), .reset(not_5_out));  // open: Qn, preset
  T_Flip_Flop t_ff_6 (.clk(t_ff_2_qn), .T(1'b1), .Q(t_ff_6_q), .reset(or_2_out));  // open: Qn, preset
  not not_8 (not_8_out, or_2_out);
  T_Flip_Flop t_ff_7 (.clk(t_ff_3_qn), .T(1'b1), .Q(t_ff_7_q), .reset(not_6_out));  // open: Qn, preset
  T_Flip_Flop t_ff_8 (.clk(t_ff_4_qn), .T(1'b1), .Q(t_ff_8_q), .reset(or_3_out));  // open: Qn, preset
  S_R_Flip_Flop #(.trigger("high")) s_r_ff_1 (
    .S(or_4_out), .clk(1'b1), .R(1'b0), .Q(s_r_ff_1_q), .reset(t_ff_9_q));  // open: Qn, preset
  // OR_Gate or_5 has open pins: in1=t_ff_10_q, out=open
  T_Flip_Flop t_ff_9 (.clk(or_1_out), .T(1'b1), .Q(t_ff_9_q), .preset(1'b0), .reset(or_4_out));  // open: Qn
  T_Flip_Flop t_ff_10 (.clk(not_7_out), .T(1'b1), .Q(t_ff_10_q), .preset(1'b0), .reset(or_4_out));  // open: Qn
  or or_6 (or_6_out, t_ff_5_q, t_ff_6_q);
  T_Flip_Flop t_ff_11 (.clk(or_2_out), .T(1'b1), .Q(t_ff_11_q), .preset(1'b0), .reset(or_6_out));  // open: Qn
  T_Flip_Flop t_ff_12 (.clk(not_8_out), .T(1'b1), .Q(t_ff_12_q), .preset(1'b0), .reset(or_6_out));  // open: Qn
  and and_4 (and_4_out, t_ff_3_q, t_ff_7_q);
  or or_7 (or_7_out, and_4_out, and_5_out);
  and and_5 (and_5_out, t_ff_8_q, t_ff_4_q);
  not not_9 (not_9_out, or_3_out);
  not not_10 (not_10_out, s_r_ff_1_q);
  LED Master_Work (.in(not_10_out));
  LED Backup_Work (.in(s_r_ff_1_q));
  _7402 N_OR (
    .pin1(Counter_Down_pin1), .pin2(or_1_out), .pin3(N_OR_pin3), .pin4(N_OR_pin4), .pin5(Counter_UP_pin15),
    .pin6(Counter_Down_pin15), .pin10(N_OR_pin10), .pin9(N_OR_pin9), .pin8(N_OR_pin8));  // open: pin13, pin12, pin11
  _7474 Restore_Trig (
    .pin1(N_OR_pin4), .pin2(Restore_Trig_pin2), .pin3(or_1_out), .pin4(Restore_Trig_pin4), .pin5(N_OR_pin9),
    .pin6(Restore_Trig_pin2), .pin13(N_OR_pin4), .pin12(Restore_Trig_pin12), .pin11(Counter_Down_pin1),
    .pin10(Restore_Trig_pin10), .pin9(N_OR_pin8), .pin8(Restore_Trig_pin12));
  S_R_Flip_Flop #(.trigger("high")) s_r_ff_2 (
    .S(or_6_out), .clk(1'b1), .R(1'b0), .Q(s_r_ff_2_q), .reset(or_8_out));  // open: Qn, preset
  or or_8 (or_8_out, t_ff_11_q, t_ff_12_q);
  S_R_Flip_Flop #(.trigger("high")) s_r_ff_3 (
    .S(or_7_out), .clk(1'b1), .R(1'b0), .Q(s_r_ff_3_q), .reset(or_9_out));  // open: Qn, preset
  or or_9 (or_9_out, t_ff_13_q, t_ff_14_q);
  T_Flip_Flop t_ff_13 (.clk(or_3_out), .T(1'b1), .Q(t_ff_13_q), .preset(1'b0), .reset(or_7_out));  // open: Qn
  T_Flip_Flop t_ff_14 (.clk(not_9_out), .T(1'b1), .Q(t_ff_14_q), .preset(1'b0), .reset(or_7_out));  // open: Qn
  Clock #(.phaseOffset(5)) clock_5 (.out(clock_5_out));
  // Digital_Oscilloscope digital_oscilloscope_1: pin names not known; wires that end beside it: clock_5_out, or_2_out, clock_2_out, s_r_ff_2_q
  not not_11 (not_11_out, s_r_ff_2_q);
  LED led_7 (.in(not_11_out));
  LED led_8 (.in(s_r_ff_2_q));
  Clock #(.phaseOffset(5)) clock_6 (.out(clock_6_out));
  // Digital_Oscilloscope digital_oscilloscope_2: pin names not known; wires that end beside it: clock_6_out, or_3_out, clock_4_out, s_r_ff_3_q
  not not_12 (not_12_out, s_r_ff_3_q);
  LED led_9 (.in(not_12_out));
  LED led_10 (.in(s_r_ff_3_q));
  _7474 Latcher (
    .pin1(N_OR_pin10), .pin2(Latcher_pin2), .pin3(Latcher_pin2), .pin4(N_OR_pin4), .pin5(Latcher_pin5));  // open: pin6, pin13, pin12, pin11, pin10, pin9, pin8
  Clock #(.phaseOffset(5)) clock_7 (.out(clock_7_out));
  // Digital_Oscilloscope digital_oscilloscope_3: pin names not known; wires that end beside it: clock_7_out, or_1_out, Backup_out, Latcher_pin5
  // also tied to GND on the sheet: {Counter_UP_pin3, Counter_Down_pin3, N_OR_pin3, Latcher_pin2}
  // also tied to VCC on the sheet: {Counter_UP_pin7, Counter_Down_pin7, Restore_Trig_pin4, Restore_Trig_pin10}

  // Notes on the sheet:
  //   Меандры лучше должны быть одинаковой частоты
  //   Размеры счетчиков зависят от разнице в частоте
  //   Счетчики
  //   Состояния постоянного 0 или 1
endmodule

module test (
);

  wire and_1_out, Backup_out, clock_1_out, counter_1_carry, counter_2_carry, dipswitch_1_sw1,
       dipswitch_1_sw2, Master_out, not_1_out, not_2_out, not_3_out, not_4_out, or_1_out, or_2_out, or_3_out,
       s_r_ff_1_q, t_ff_1_q, t_ff_2_q;

  Clock #(.highDuration(6), .lowDuration(6)) Master (.out(Master_out));
  Clock Backup (.out(Backup_out));
  not not_1 (not_1_out, dipswitch_1_sw1);
  DipSwitch #(.number(2)) dipswitch_1 (.sw1(dipswitch_1_sw1), .sw2(dipswitch_1_sw2));
  and and_1 (and_1_out, Master_out, not_1_out);
  or or_1 (or_1_out, and_1_out, dipswitch_1_sw2);
  LED led_1 (.in(or_1_out));
  LED led_2 (.in(Backup_out));
  Counter #(.max('hf), .width(4)) counter_1 (
    .carry(counter_1_carry), .clk(Backup_out), .clr(not_2_out));  // open: load, D, count, Q, up
  not not_2 (not_2_out, or_1_out);
  Counter #(.max('hf), .width(4)) counter_2 (
    .carry(counter_2_carry), .clk(Backup_out), .clr(or_1_out));  // open: load, D, count, Q, up
  or or_2 (or_2_out, counter_1_carry, counter_2_carry);
  not not_3 (not_3_out, or_1_out);
  S_R_Flip_Flop #(.trigger("high")) s_r_ff_1 (
    .S(or_2_out), .clk(1'b1), .R(1'b0), .Q(s_r_ff_1_q), .reset(or_3_out));  // open: Qn, preset
  or or_3 (or_3_out, t_ff_1_q, t_ff_2_q);
  T_Flip_Flop t_ff_1 (.clk(or_1_out), .T(1'b1), .Q(t_ff_1_q), .preset(1'b0), .reset(or_2_out));  // open: Qn
  T_Flip_Flop t_ff_2 (.clk(not_3_out), .T(1'b1), .Q(t_ff_2_q), .preset(1'b0), .reset(or_2_out));  // open: Qn
  Clock #(.phaseOffset(5)) clock_1 (.out(clock_1_out));
  // Digital_Oscilloscope digital_oscilloscope_1: pin names not known; wires that end beside it: clock_1_out, or_1_out, Backup_out, s_r_ff_1_q
  not not_4 (not_4_out, s_r_ff_1_q);
  LED Master_Work (.in(not_4_out));
  LED Backup_Work (.in(s_r_ff_1_q));

  // Notes on the sheet:
  //   Состояния постоянного 0 или 1
  //   Меандры лучше должны быть одинаковой частоты
  //   Размеры счетчиков зависят от разнице в частоте
  //   Счетчики
endmodule

module Arbiter (
  output Control
);

  wire Backup_out, Counter_Down_pin1, Counter_Down_pin15, Counter_UP_pin3, Counter_UP_pin7, Counter_UP_pin15,
       Latcher_pin2, Master_out, N_OR_pin4;

  Clock #(.highDuration(6), .lowDuration(6)) Master (.out(Master_out));
  Clock #(.highDuration(2), .lowDuration(2)) Backup (.out(Backup_out));
  _74161 Counter_UP (
    .pin1(Master_out), .pin2(Backup_out), .pin3(Counter_UP_pin3), .pin4(Counter_UP_pin3),
    .pin5(Counter_UP_pin3), .pin6(Counter_UP_pin3), .pin7(Counter_UP_pin7), .pin15(Counter_UP_pin15),
    .pin10(Counter_UP_pin7), .pin9(Counter_UP_pin7));  // open: pin14, pin13, pin12, pin11
  _74161 Counter_Down (
    .pin1(Counter_Down_pin1), .pin2(Backup_out), .pin3(Counter_UP_pin3), .pin4(Counter_UP_pin3),
    .pin5(Counter_UP_pin3), .pin6(Counter_UP_pin3), .pin7(Counter_UP_pin7), .pin15(Counter_Down_pin15),
    .pin10(Counter_UP_pin7), .pin9(Counter_UP_pin7));  // open: pin14, pin13, pin12, pin11
  _7402 N_OR (
    .pin1(Counter_Down_pin1), .pin2(Master_out), .pin3(Counter_UP_pin3), .pin4(N_OR_pin4),
    .pin5(Counter_UP_pin15), .pin6(Counter_Down_pin15));  // open: pin13, pin12, pin11, pin10, pin9, pin8
  _7474 Latcher (
    .pin1(N_OR_pin4), .pin2(Latcher_pin2), .pin3(Master_out), .pin4(Counter_UP_pin7), .pin6(Latcher_pin2),
    .pin13(Latcher_pin2), .pin12(Counter_UP_pin3), .pin11(Counter_UP_pin3), .pin10(N_OR_pin4), .pin9(Control));  // open: pin5, pin8
  // also tied to GND on the sheet: Counter_UP_pin3
  // also tied to VCC on the sheet: Counter_UP_pin7
endmodule

module test2 (
);

  wire and_1_out, Backup_out, clock_1_out, counter_1_carry, counter_2_carry, d_ff_1_qn, d_ff_2_q,
       dipswitch_1_sw1, dipswitch_1_sw2, Master_out, nor_1_out, nor_2_out, not_1_out, not_2_out, not_3_out,
       not_4_out, not_5_out, not_6_out, or_1_out;

  Clock #(.highDuration(6), .lowDuration(6)) Master (.out(Master_out));
  Clock Backup (.out(Backup_out));
  not not_1 (not_1_out, dipswitch_1_sw1);
  DipSwitch #(.number(2)) dipswitch_1 (.sw1(dipswitch_1_sw1), .sw2(dipswitch_1_sw2));
  and and_1 (and_1_out, Master_out, not_1_out);
  or or_1 (or_1_out, and_1_out, dipswitch_1_sw2);
  LED led_1 (.in(or_1_out));
  LED led_2 (.in(Backup_out));
  Counter #(.max('hf), .width(4)) counter_1 (
    .carry(counter_1_carry), .clk(Backup_out), .clr(nor_1_out));  // open: load, D, count, Q, up
  nor nor_1 (nor_1_out, or_1_out, or_1_out);
  Counter #(.max('hf), .width(4)) counter_2 (
    .carry(counter_2_carry), .clk(Backup_out), .clr(or_1_out));  // open: load, D, count, Q, up
  not not_2 (not_2_out, 1'b1);
  not not_3 (not_3_out, nor_2_out);
  nor nor_2 (nor_2_out, counter_1_carry, counter_2_carry);
  D_Flip_Flop d_ff_1 (.clk(or_1_out), .D(d_ff_1_qn), .Qn(d_ff_1_qn), .preset(not_2_out), .reset(not_3_out));  // open: Q
  D_Flip_Flop d_ff_2 (.clk(1'b0), .D(1'b0), .Q(d_ff_2_q), .preset(not_4_out), .reset(not_5_out));  // open: Qn
  not not_4 (not_4_out, nor_2_out);
  not not_5 (not_5_out, d_ff_1_qn);
  Clock #(.phaseOffset(5)) clock_1 (.out(clock_1_out));
  // Digital_Oscilloscope digital_oscilloscope_1: pin names not known; wires that end beside it: clock_1_out, or_1_out, Backup_out, d_ff_2_q
  not not_6 (not_6_out, d_ff_2_q);
  LED Master_Work (.in(not_6_out));
  LED Backup_Work (.in(d_ff_2_q));

  // Notes on the sheet:
  //   Состояния постоянного 0 или 1
  //   Меандры лучше должны быть одинаковой частоты
  //   Размеры счетчиков зависят от разнице в частоте
  //   Счетчики
endmodule
